// Logisim project ULA.circ as structural Verilog: 4 circuits, main circuit main
module main (
  input  [31:0] Entrada_A,
  input  [31:0] Entrada_B,
  input  [31:0] \Saída_S ,
  input  [4:0] Seletor,
  output Overflow
);

  wire celulaula_1_cout, celulaula_3_cout, celulaula_4_cout, celulaula_5_cout, celulaula_6_cout,
       celulaula_7_cout, celulaula_8_cout, celulaula_9_cout, celulaula_10_cout, celulaula_11_cout,
       celulaula_12_cout, celulaula_13_cout, celulaula_14_cout, celulaula_15_cout, celulaula_17_cout,
       celulaula_18_cout, celulaula_19_cout, celulaula_20_cout, celulaula_21_cout, celulaula_22_cout,
       celulaula_23_cout, celulaula_24_cout, celulaula_25_cout, celulaula_26_cout, celulaula_27_cout,
       celulaula_28_cout, celulaula_29_cout, celulaula_30_cout, celulaula_31_cout, celulaula_32_cout,
       Overflow_p1, Overflow_p2;

  // OverFlowControler Overflow: pin names not known; wires that end beside it: Overflow_p1, Overflow_p2, Seletor, Entrada_A[31], Entrada_B[31]
  CelulaULA celulaula_1 (
    .a(Entrada_A[31]), .b(Entrada_B[31]), .Cin(1'b0), .Seletor(Seletor), .S(\Saída_S [31]),
    .Cout(celulaula_1_cout));
  CelulaULA celulaula_2 (
    .a(Entrada_A[31]), .b(Entrada_B[31]), .Cin(celulaula_4_cout), .Seletor(Seletor), .S(\Saída_S [31]),
    .Cout(Overflow_p2));
  CelulaULA celulaula_3 (
    .a(Entrada_A[31]), .b(Entrada_B[31]), .Cin(celulaula_1_cout), .Seletor(Seletor), .S(\Saída_S [31]),
    .Cout(celulaula_3_cout));
  CelulaULA celulaula_4 (
    .a(Entrada_A[31]), .b(Entrada_B[31]), .Cin(celulaula_6_cout), .Seletor(Seletor), .S(\Saída_S [31]),
    .Cout(celulaula_4_cout));
  CelulaULA celulaula_5 (
    .a(Entrada_A[31]), .b(Entrada_B[31]), .Cin(celulaula_3_cout), .Seletor(Seletor), .S(\Saída_S [31]),
    .Cout(celulaula_5_cout));
  CelulaULA celulaula_6 (
    .a(Entrada_A[31]), .b(Entrada_B[31]), .Cin(celulaula_8_cout), .Seletor(Seletor), .S(\Saída_S [31]),
    .Cout(celulaula_6_cout));
  CelulaULA celulaula_7 (
    .a(Entrada_A[31]), .b(Entrada_B[31]), .Cin(celulaula_5_cout), .Seletor(Seletor), .S(\Saída_S [31]),
    .Cout(celulaula_7_cout));
  CelulaULA celulaula_8 (
    .a(Entrada_A[31]), .b(Entrada_B[31]), .Cin(celulaula_10_cout), .Seletor(Seletor), .S(\Saída_S [31]),
    .Cout(celulaula_8_cout));
  CelulaULA celulaula_9 (
    .a(Entrada_A[31]), .b(Entrada_B[31]), .Cin(celulaula_7_cout), .Seletor(Seletor), .S(\Saída_S [31]),
    .Cout(celulaula_9_cout));
  CelulaULA celulaula_10 (
    .a(Entrada_A[31]), .b(Entrada_B[31]), .Cin(celulaula_12_cout), .Seletor(Seletor), .S(\Saída_S [31]),
    .Cout(celulaula_10_cout));
  CelulaULA celulaula_11 (
    .a(Entrada_A[31]), .b(Entrada_B[31]), .Cin(celulaula_9_cout), .Seletor(Seletor), .S(\Saída_S [31]),
    .Cout(celulaula_11_cout));
  CelulaULA celulaula_12 (
    .a(Entrada_A[31]), .b(Entrada_B[31]), .Cin(celulaula_14_cout), .Seletor(Seletor), .S(\Saída_S [31]),
    .Cout(celulaula_12_cout));
  CelulaULA celulaula_13 (
    .a(Entrada_A[31]), .b(Entrada_B[31]), .Cin(celulaula_11_cout), .Seletor(Seletor), .S(\Saída_S [31]),
    .Cout(celulaula_13_cout));
  CelulaULA celulaula_14 (
    .a(Entrada_A[31]), .b(Entrada_B[31]), .Seletor(Seletor), .S(\Saída_S [31]), .Cout(celulaula_14_cout));  // open: Cin
  CelulaULA celulaula_15 (
    .a(Entrada_A[31]), .b(Entrada_B[31]), .Cin(celulaula_13_cout), .Seletor(Seletor), .S(\Saída_S [31]),
    .Cout(celulaula_15_cout));
  CelulaULA celulaula_16 (
    .a(Entrada_A[31]), .b(Entrada_B[31]), .Cin(celulaula_18_cout), .Seletor(Seletor), .S(\Saída_S [31]));  // open: Cout
  CelulaULA celulaula_17 (
    .a(Entrada_A[31]), .b(Entrada_B[31]), .Cin(celulaula_15_cout), .Seletor(Seletor), .S(\Saída_S [31]),
    .Cout(celulaula_17_cout));
  CelulaULA celulaula_18 (
    .a(Entrada_A[31]), .b(Entrada_B[31]), .Cin(celulaula_20_cout), .Seletor(Seletor), .S(\Saída_S [31]),
    .Cout(celulaula_18_cout));
  CelulaULA celulaula_19 (
    .a(Entrada_A[31]), .b(Entrada_B[31]), .Cin(celulaula_17_cout), .Seletor(Seletor), .S(\Saída_S [31]),
    .Cout(celulaula_19_cout));
  CelulaULA celulaula_20 (
    .a(Entrada_A[31]), .b(Entrada_B[31]), .Cin(celulaula_22_cout), .Seletor(Seletor), .S(\Saída_S [31]),
    .Cout(celulaula_20_cout));
  CelulaULA celulaula_21 (
    .a(Entrada_A[31]), .b(Entrada_B[31]), .Cin(celulaula_19_cout), .Seletor(Seletor), .S(\Saída_S [31]),
    .Cout(celulaula_21_cout));
  CelulaULA celulaula_22 (
    .a(Entrada_A[31]), .b(Entrada_B[31]), .Cin(celulaula_24_cout), .Seletor(Seletor), .S(\Saída_S [31]),
    .Cout(celulaula_22_cout));
  CelulaULA celulaula_23 (
    .a(Entrada_A[31]), .b(Entrada_B[31]), .Cin(celulaula_21_cout), .Seletor(Seletor), .S(\Saída_S [31]),
    .Cout(celulaula_23_cout));
  CelulaULA celulaula_24 (
    .a(Entrada_A[31]), .b(Entrada_B[31]), .Cin(celulaula_26_cout), .Seletor(Seletor), .S(\Saída_S [31]),
    .Cout(celulaula_24_cout));
  CelulaULA celulaula_25 (
    .a(Entrada_A[31]), .b(Entrada_B[31]), .Cin(celulaula_23_cout), .Seletor(Seletor), .S(\Saída_S [31]),
    .Cout(celulaula_25_cout));
  CelulaULA celulaula_26 (
    .a(Entrada_A[31]), .b(Entrada_B[31]), .Cin(celulaula_28_cout), .Seletor(Seletor), .S(\Saída_S [31]),
    .Cout(celulaula_26_cout));
  CelulaULA celulaula_27 (
    .a(Entrada_A[31]), .b(Entrada_B[31]), .Cin(celulaula_25_cout), .Seletor(Seletor), .S(\Saída_S [31]),
    .Cout(celulaula_27_cout));
  CelulaULA celulaula_28 (
    .a(Entrada_A[31]), .b(Entrada_B[31]), .Cin(celulaula_30_cout), .Seletor(Seletor), .S(\Saída_S [31]),
    .Cout(celulaula_28_cout));
  CelulaULA celulaula_29 (
    .a(Entrada_A[31]), .b(Entrada_B[31]), .Cin(celulaula_27_cout), .Seletor(Seletor), .S(\Saída_S [31]),
    .Cout(celulaula_29_cout));
  CelulaULA celulaula_30 (
    .a(Entrada_A[31]), .b(Entrada_B[31]), .Cin(celulaula_32_cout), .Seletor(Seletor), .S(\Saída_S [31]),
    .Cout(celulaula_30_cout));
  CelulaULA celulaula_31 (
    .a(Entrada_A[31]), .b(Entrada_B[31]), .Cin(celulaula_29_cout), .Seletor(Seletor), .S(\Saída_S [31]),
    .Cout(celulaula_31_cout));
  CelulaULA celulaula_32 (
    .a(Entrada_A[31]), .b(Entrada_B[31]), .Cin(celulaula_31_cout), .Seletor(Seletor), .S(\Saída_S [31]),
    .Cout(celulaula_32_cout));

  assign Entrada_A[30:0] = {31{Entrada_A[31]}};
  assign Entrada_B[30:0] = {31{Entrada_B[31]}};
  assign \Saída_S [30:0] = {31{\Saída_S [31]}};
endmodule

module Somador (
  input  a,
  input  b,
  input  Cin,
  output Cout,
  output s
);

  wire and_1_out, and_2_out, and_3_out, and_4_out, xor_2_out;

  xor xor_1 (s, Cin, xor_2_out);
  xor xor_2 (xor_2_out, a, b);
  and and_1 (and_1_out, ~Cin, a, b);  // AND_Gate
  and and_2 (and_2_out, Cin, ~a, b);  // AND_Gate
  and and_3 (and_3_out, Cin, a, ~b);  // AND_Gate
  and and_4 (and_4_out, Cin, a, b);
  or or_1 (Cout, and_1_out, and_2_out, and_3_out, and_4_out);
endmodule

// Celula
module CelulaULA (
  input  a,
  input  b,
  input  Cin,
  input  [4:0] Seletor,
  output S,
  output Cout
);

  wire and_1_out, nand_1_out, or_1_out, somador_1_s, xor_1_out;

  and and_1 (and_1_out, a, b);
  or or_1 (or_1_out, a, b);
  xor xor_1 (xor_1_out, a, b);
  nand nand_1 (nand_1_out, a, b);
  Somador somador_1 (.Cin(Cin), .a(b), .b(a), .s(somador_1_s), .Cout(Cout));
  Multiplexer #(.select(5), .enable("false")) multiplexer_1 (
    .in0(and_1_out), .in1(or_1_out), .in2(xor_1_out), .in3(nand_1_out), .in4(somador_1_s), .in5(somador_1_s),
    .out(S), .sel(Seletor));  // open: in6, in7, in8, in9, in10, in11, in12, in13, in14, in15, in16, in17, in18, in19, in20, in21, in22, in23, in24, in25, in26, in27, in28, in29, in30, in31

  // Notes on the sheet:
  //   00000=AND
  //   00001=OR
  //   00010=XOR
  //   00011=NAND
  //   00100=SOMA INT
  //   00101=SOMA NAT
endmodule

module OverFlowControler (
  input  CoutMSB,
  input  a,
  input  b,
  input  s,
  input  [2:0] in_5,
  input  [4:0] Seletor,
  output Overflow
);

  wire and_1_out, and_2_out, and_3_out, or_1_out;
  wire [4:0] undriven;

  Multiplexer #(.select(5), .enable("false")) multiplexer_1 (
    .in15(CoutMSB), .in17(or_1_out), .in24(and_1_out), .out(Overflow), .sel(undriven));  // open: in0, in1, in2, in3, in4, in5, in6, in7, in8, in9, in10, in11, in12, in13, in14, in16, in18, in19, in20, in21, in22, in23, in25, in26, in27, in28, in29, in30, in31
  and and_1 (and_1_out, in_5[0], ~in_5[1], in_5[2]);  // AND_Gate
  or or_1 (or_1_out, and_2_out, and_3_out);
  and and_2 (and_2_out, a, b, ~s);  // AND_Gate
  and and_3 (and_3_out, ~a, ~b, s);  // AND_Gate
endmodule
